# Fritzing sketch Car Board (saved by Fritzing 0.9.3b)
perfboards: 1

parts:
  Part1 = Arduino Nano (Rev3.0) (ICSP)
  Part2 = NRF24L01+ Breakout Board
  IC1 = L293D [package=THT]  # not connected
  M1 = DC Motor  # not connected
  M2 = DC Motor  # not connected
  BAT1 = BC9VPC [package=bc9vpc]  # not connected
  C1 = Electrolytic Capacitor [capacitance=10µF voltage=10V package="100 mil [THT, electrolytic]"]
  LED1 = LEDs [package=led10mm]
  LED2 = LEDs [package=led10mm]

nets:
  N1: Part1.A1, LED1.A
  N2: Part1.A0, LED2.A
  N3: Part2.GND, C1.-
  N4: Part2.VCC, C1.+
  N5: LED1.C, LED2.C
